# Fritzing sketch 555_button (saved by Fritzing 0.8.0b)
breadboards: 1

parts:
  R1 = Resistor [tolerance=±5% resistance=10k package=THT]
  VCC1 = Battery
  LED1 = LED - 5mm [color="Red (633nm)" package="5 mm [THT]"]
  S1 = Pushbutton [package="[THT]"]
  IC1 = IC, DIP package, 8 pins [chip_label=IC]
  C1 = Electrolytic Capacitor [capacitance=47µF package="100 mil [THT, electrolytic]"]
  R2 = Resistor [tolerance=±5% resistance=470 package=THT]
  R3 = Resistor [tolerance=±5% resistance=220 package=THT]
  C2 = Capacitor [package=grm43d]  # not connected
  C3 = Capacitor [package=grm43d]  # not connected
  Y1 = Resonator [frequency="16 Mhz" package=THT]

nets:
  N1: R1.Pin_0, IC1.pin6, IC1.pin7, C1.+
  N2: R1.Pin_1, VCC1.+, IC1.pin8, R3.Pin_0
  N3: VCC1.-, S1.Pin_1, S1.Pin_2, IC1.pin1, C1.-, R2.Pin_0, Y1.0
  N4: LED1.cathode, R2.Pin_1
  N5: LED1.anode, IC1.pin3
  N6: S1.Pin_3, S1.Pin_4, IC1.pin2, R3.Pin_1
  N7: IC1.pin5, Y1.1
