# Fritzing sketch 555_reset_buttons (saved by Fritzing 0.8.0b)
breadboards: 1

parts:
  VCC1 = Battery
  LED1 = LED - 5mm [color="Red (633nm)" package="5 mm [THT]"]
  S1 = Pushbutton [package="[THT]"]
  IC1 = IC, DIP package, 8 pins [chip_label=IC]
  R2 = Resistor [tolerance=±5% resistance=470 package=THT]
  C2 = Capacitor [package=grm43d]  # not connected
  C3 = Capacitor [package=grm43d]  # not connected
  Y1 = Resonator [frequency="16 Mhz" package=THT]
  R4 = Resistor [tolerance=±5% resistance=10k package=THT]
  R6 = Resistor [tolerance=±5% resistance=10k package=THT]
  S3 = Pushbutton [package="[THT]"]

nets:
  N1: VCC1.-, S1.Pin_3, S1.Pin_4, IC1.pin1, IC1.pin6, R2.Pin_0, Y1.0, S3.Pin_3, S3.Pin_4
  N2: VCC1.+, IC1.pin8, R4.Pin_0, R6.Pin_0
  N3: LED1.cathode, R2.Pin_1
  N4: LED1.anode, IC1.pin3
  N5: S1.Pin_1, S1.Pin_2, IC1.pin4, R4.Pin_1
  N6: IC1.pin2, R6.Pin_1, S3.Pin_1, S3.Pin_2
  N7: IC1.pin5, Y1.1
