# Fritzing sketch circuit_LED_pot_battery (saved by Fritzing 0.8.0b)
breadboards: 1

parts:
  R1 = Resistor [tolerance=±5% resistance=220 package=THT]
  VCC1 = Battery
  U1 = POT [package=pot_alpha_rv16af-20]
  LED1 = LEDs [color="Red (633nm)" package=fkit-led-1206]  # not connected
  LED2 = LED - 5mm [color="Red (633nm)" package="5 mm [THT]"]

nets:
  N1: R1.Pin_0, LED2.anode
  N2: R1.Pin_1, VCC1.-, U1.E
  N3: VCC1.+, U1.A
  N4: U1.S, LED2.cathode
