# Fritzing sketch 555_pot (saved by Fritzing 0.8.0b)
breadboards: 1

parts:
  R1 = Resistor [tolerance=±5% resistance=10k package=THT]
  VCC1 = Battery
  IC1 = IC, DIP package, 8 pins [chip_label=IC]
  C1 = Electrolytic Capacitor [capacitance=47µF package="100 mil [THT, electrolytic]"]
  C2 = Capacitor [package=grm43d]  # not connected
  C3 = Capacitor [package=grm43d]  # not connected
  Y1 = Resonator [frequency="16 Mhz" package=THT]
  U1 = POT [package=pot_mammoth]
  J1 = Piezo Speaker

nets:
  N1: R1.Pin_0, IC1.pin2, IC1.pin6, C1.+, U1.A
  N2: R1.Pin_1, IC1.pin7
  N3: VCC1.-, IC1.pin1, C1.-, Y1.0, J1.pin1
  N4: VCC1.+, IC1.pin4, IC1.pin8, U1.S
  N5: IC1.pin3, J1.pin2
  N6: IC1.pin5, Y1.1
