# Fritzing sketch circuit_LED_pot_battery (saved by Fritzing 0.8.0b)
breadboards: 1

parts:
  R1 = Resistor [tolerance=±5% resistance=220 package=THT]
  VCC1 = Battery
  LED1 = LED - 5mm [color="Red (633nm)" package="5 mm [THT]"]
  U1 = POT [package=pot_alpha_rv16af-20]

nets:
  N1: R1.Pin_0, LED1.anode, U1.S
  N2: VCC1.-, LED1.cathode, U1.E
  N3: VCC1.+, U1.A
